# Fritzing sketch WindSensor (saved by Fritzing 0.9.4)
breadboards: 1

parts:
  ABX00014 = Arduino MKR Fox 1200
  S1 = SWITCH-MOMENTARY-2 [package=reed_switch_pth]
  S3 = SWITCH-MOMENTARY-2 [package=reed_switch_pth]
  R1 = Resistor [tolerance=±1% resistance=33k package=THT]
  S4 = SWITCH-MOMENTARY-2 [package=reed_switch_pth]
  S5 = SWITCH-MOMENTARY-2 [package=reed_switch_pth]
  S6 = SWITCH-MOMENTARY-2 [package=reed_switch_pth]
  S7 = SWITCH-MOMENTARY-2 [package=reed_switch_pth]
  S8 = SWITCH-MOMENTARY-2 [package=reed_switch_pth]
  S2 = SWITCH-MOMENTARY-2 [package=reed_switch_pth]
  R2 = Resistor [tolerance=±1% resistance=8.2k package=THT]
  R3 = Resistor [tolerance=±1% resistance=1k package=THT]
  R4 = Resistor [tolerance=±1% resistance=2.2k package=THT]
  R5 = Resistor [tolerance=±1% resistance=3.9k package=THT]
  R6 = Resistor [tolerance=±1% resistance=16k package=THT]
  R7 = Resistor [tolerance=±1% resistance=120k package=THT]
  R8 = Resistor [tolerance=±1% resistance=64.9k package=THT]
  R9 = Resistor [tolerance=±1% resistance=10k package=THT]
  S9 = SWITCH-MOMENTARY-2 [package=reed_switch_pth]
  RJ11 = RJ11 Jack [package=rj11-6]
  VCC1 = Battery
  U1 = TVS [package=sma-diode]
  U2 = TVS [package=sma-diode]

nets:
  pinGirAdc: ABX00014.A6, S1.2, S3.2, S4.2, S5.2, S6.2, S7.2, S8.2, S2.2, R9.Pin_0, RJ11.4, U1.1
  intPinAnemo: ABX00014.~4, S9.2, RJ11.5, U2.1
  pinGirAlim: ABX00014.~5, R9.Pin_1
  GND: ABX00014.GND, R1.Pin_1, R2.Pin_1, R3.Pin_1, R4.Pin_1, R5.Pin_1, R6.Pin_1, R7.Pin_1, R8.Pin_1, S9.1, RJ11.2, RJ11.3, VCC1.-, U1.2, U2.2
  N1: ABX00014.VIN, VCC1.+
  N2: S1.1, R1.Pin_0
  N3: S3.1, R3.Pin_0
  N4: S4.1, R4.Pin_0
  N5: S5.1, R5.Pin_0
  N6: S6.1, R6.Pin_0
  N7: S7.1, R7.Pin_0
  N8: S8.1, R8.Pin_0
  N9: S2.1, R2.Pin_0

notes:
  ref WH-SP-WD
  ref WH-SP-WS

custom parts:
  Battery: Your standard 2x 18650 battery pack (7,4 Volts)
