# Fritzing sketch WindSensorMKR (saved by Fritzing 0.9.9b)
circuit board: 8.8cm x 4.6cm

parts:
  R1 = Resistor [tolerance=±1% resistance=10k power=0.25 package=THT]
  R3_560kΩ = Resistor [tolerance=±1% resistance=560k power=0.25 package=THT]
  R4_390kΩ = Resistor [tolerance=±1% resistance=390k power=0.25 package=THT]
  C2 = Film/Foil Capacitor [capacitance=100nF voltage=35V package="5mm [THT, pp]"]
  C1 = Film/Foil Capacitor [capacitance=100nF voltage=35V package="5mm [THT, pp]"]
  D1 = Schottky Diode [part_number=1N5817 package="300 mil [THT]"]
  D2 = Schottky Diode [part_number=1N5817 package="300 mil [THT]"]
  D3 = Schottky Diode [part_number=1N5817 package="300 mil [THT]"]
  D4 = Schottky Diode [part_number=1N5817 package="300 mil [THT]"]
  R2 = Resistor [tolerance=±1% resistance=100k power=0.25 package=THT]
  R5 = Resistor [tolerance=±1% resistance=1k power=0.25 package=THT]
  R6 = Resistor [tolerance=±1% resistance=1k power=0.25 package=THT]
  RJ11_MISOL = RJ11 Jack [package=rj11-6]
  BME280 = BME280 Barometric Sensor
  TP4056 = TP4056 [chip_label=TP4056 package="DIP (Dual Inline) [THT]"]
  MKRFox1200 = Arduino MKR Fox 1200
  tp- = female pin header, 1 pin [form="♀ (female)"]
  tpS+ = female pin header, 1 pin [form="♀ (female)"]
  tpbat = female pin header, 1 pin [form="♀ (female)"]
  J1 = JST XH 2A male [form="♀ (female)"]
  +BAT- = JST XH 2A male [form="♀ (female)"]
  +SOLAR- = JST XH 2A male [form="♀ (female)"]
  ON/OFF = prefix0001

nets:
  pinGirAdc: R1.Pin_0, C2.-, D2.cathode, D3.anode, R6.Pin_0, MKRFox1200.A6
  pinGirAlim: R1.Pin_1, D3.cathode, MKRFox1200.~5
  N1: R3_560kΩ.Pin_0, R4_390kΩ.Pin_1, MKRFox1200.A4
  Vbat: R3_560kΩ.Pin_1, TP4056.pin4, tpbat.pin1, +BAT-.pin2
  GND: R4_390kΩ.Pin_0, C2.+, C1.+, D1.anode, D2.anode, RJ11_MISOL.4, RJ11_MISOL.5, TP4056.pin2, TP4056.pin5, TP4056.pin6, MKRFox1200.GND, tp-.pin1, +BAT-.pin1, +SOLAR-.pin1
  intPinAnemo: C1.-, D1.cathode, D4.anode, R2.Pin_1, R5.Pin_0, MKRFox1200.~4
  Vcc: D4.cathode, R2.Pin_0, MKRFox1200.VCC
  N2: R5.Pin_1, RJ11_MISOL.3
  N3: R6.Pin_1, RJ11_MISOL.2
  pinGndBME: BME280.GND, MKRFox1200.10_MISO
  pinVccBME: BME280.VCC, MKRFox1200.9_SCK
  SCL: BME280.SCL, MKRFox1200.12_SCL
  SDA: BME280.SDA, MKRFox1200.11_SDA
  N4: TP4056.pin1, tpS+.pin1, +SOLAR-.pin2
  N5: TP4056.pin3, J1.pin2, ON/OFF.connector1, ON/OFF.connector2
  N6: MKRFox1200.VIN, J1.pin1, ON/OFF.connector0

notes:
  yellow
  green
  red
  black
  WindSensorMKR1200

custom parts:
  RJ11 Jack: RJ11 Jack6 pin RJ11 jack stright
  BME280 Barometric Sensor: Bosh BME280 pressure temperature humidity
  JST XH 2A male: 2.54mm
